# Fritzing sketch WeatherSensor (saved by Fritzing 0.9.3b)
breadboards: 1

parts:
  VCC1 = 4 x AAA Battery Mount
  LED1 = smd LED [color="Green (555nm)" package="0805 [SMD]"]
  S4 = Round Pushbutton
  DHT1 = DHT22 Humidity and Temperature Sensor
  R1 = Resistor [tolerance=±5% resistance=10k package="2010 [SMD]"]
  R2 = Resistor [tolerance=±5% resistance=220 package=THT]
  U1 = NodeMCU V1.0

nets:
  GND: VCC1.-, LED1.anode, S4.leg1, DHT1.GND, U1.GND
  N1: VCC1.+, U1.Vin
  N2: LED1.cathode, R2.Pin_0
  N3: S4.leg0, U1.D6
  VDD: DHT1.VDD, R1.Pin_0, U1.3V3
  N4: DHT1.DATA, R1.Pin_1, U1.D2
  N5: R2.Pin_1, U1.D3

custom parts:
  NodeMCU V1.0: ESP8266 based NodeMCU
